# Fritzing sketch Saldivar-Joseph-Final_Project (saved by Fritzing 0.9.2b)
perfboards: 1

parts:
  U3 = TMP36 [package=to-92-kit]
  CHARGER1 = USB_LiIon_LiPoly_Charger_v1.2  # not connected
  BATT1 = LiPoly Battery (1300mAh)  # not connected
  Part1 = Solar Cell  # not connected
  C2 = Electrolytic Capacitor [capacitance=100µF package="200 mil [THT, electrolytic]"]  # not connected
  U4 = XBee

nets:
  N1: U3.VOUT, U4.pin20

custom parts:
  LiPoly Battery (1300mAh): Lithium Ion Polymer Battery (1300mAh)
