# Fritzing sketch siron-craig-finalproject (saved by Fritzing 0.9.2b)
breadboards: 1

parts:
  U1 = XBEE-1 [package=xbee-1]
  Part1 = Arduino Uno (Rev3)
  neopixel2 = Neopixel Ring 16

nets:
  3V3: U1.DOUT, Part1.3V3, neopixel2.VCC
  N1: U1.DIN, Part1.D0/RX
  N2: U1.DIO12, Part1.D1/TX
  GND: U1.GND, Part1.GND, neopixel2.GND
  N3: Part1.D6_PWM, neopixel2.IN

custom parts:
  Neopixel Ring 16: Neopixel Ring x16
